// Logisim project STL_Part1.circ as structural Verilog: 7 circuits, main circuit main
module main (
  input  [3:0] in_1,
  input  [3:0] in_2,
  input  [2:0] _0_AND____1_OR____2_XOR____3_NAND____4_NOR____5_XNOR____6_ADD____7_SUB,
  input  _0_BIN_O_P____1_GRAY_CODE_O_P,
  output [3:0] out_5
);

  wire [3:0] and_1_out_3, and_2_out_3, btogc_1_out_2, multiplexer_1_out, n4bas_1_y, n4bas_2_y, not_1_out,
       not_2_out, not_3_out, or_1_out_3, or_2_out_3, xor_1_out_3, xor_2_out_3;

  AND and_1 (.in_1(in_1), .in_2(in_2), .out_3(and_1_out_3));
  OR or_1 (.in_1(in_1), .in_2(in_2), .out_3(or_1_out_3));
  XOR xor_1 (.in_1(in_1), .in_2(in_2), .out_3(xor_1_out_3));
  AND and_2 (.in_1(in_1), .in_2(in_2), .out_3(and_2_out_3));
  OR or_2 (.in_1(in_1), .in_2(in_2), .out_3(or_2_out_3));
  XOR xor_2 (.in_1(in_1), .in_2(in_2), .out_3(xor_2_out_3));
  _4BAS u_4bas_1 (.B(in_2), .Sel(1'b0), .A(in_1), .Y(n4bas_1_y));  // open: Coutf
  _4BAS u_4bas_2 (.B(in_2), .Sel(1'b1), .A(in_1), .Y(n4bas_2_y));  // open: Coutf
  assign not_1_out = ~and_2_out_3;  // NOT_Gate not_1, 4 bits wide
  assign not_2_out = ~or_2_out_3;  // NOT_Gate not_2, 4 bits wide
  assign not_3_out = ~xor_2_out_3;  // NOT_Gate not_3, 4 bits wide
  Multiplexer #(.select(3), .width(4)) multiplexer_1 (
    .in0(and_1_out_3), .in1(or_1_out_3), .in2(xor_1_out_3), .in3(not_1_out), .in4(not_2_out),
    .in5(not_3_out), .in6(n4bas_1_y), .in7(n4bas_2_y), .out(multiplexer_1_out),
    .sel(_0_AND____1_OR____2_XOR____3_NAND____4_NOR____5_XNOR____6_ADD____7_SUB));  // open: en
  BtoGC btogc_1 (.in_1(multiplexer_1_out), .out_2(btogc_1_out_2));
  Multiplexer #(.width(4)) multiplexer_2 (
    .in0(multiplexer_1_out), .in1(btogc_1_out_2), .out(out_5), .sel(_0_BIN_O_P____1_GRAY_CODE_O_P));  // open: en
endmodule

module AND (
  input  [3:0] in_1,
  input  [3:0] in_2,
  output [3:0] out_3
);

  and and_1 (out_3[0], in_1[0], in_2[0]);
  and and_2 (out_3[1], in_1[1], in_2[1]);
  and and_3 (out_3[2], in_1[2], in_2[2]);
  and and_4 (out_3[3], in_1[3], in_2[3]);
endmodule

module OR (
  input  [3:0] in_1,
  input  [3:0] in_2,
  output [3:0] out_3
);

  or or_1 (out_3[0], in_1[0], in_2[0]);
  or or_2 (out_3[1], in_1[1], in_2[1]);
  or or_3 (out_3[2], in_1[2], in_2[2]);
  or or_4 (out_3[3], in_1[3], in_2[3]);
endmodule

module XOR (
  input  [3:0] in_1,
  input  [3:0] in_2,
  output [3:0] out_3
);

  xor xor_1 (out_3[0], in_1[0], in_2[0]);
  xor xor_2 (out_3[1], in_1[1], in_2[1]);
  xor xor_3 (out_3[2], in_1[2], in_2[2]);
  xor xor_4 (out_3[3], in_1[3], in_2[3]);
endmodule

module FA (
  input  A,
  input  B,
  input  Cin,
  output Y,
  output Cout
);

  wire and_1_out, and_2_out, xor_1_out;

  xor xor_1 (xor_1_out, A, B);
  xor xor_2 (Y, xor_1_out, Cin);
  and and_1 (and_1_out, Cin, xor_1_out);
  and and_2 (and_2_out, A, B);
  or or_1 (Cout, and_1_out, and_2_out);
endmodule

module _4BAS (
  input  [3:0] B,
  input  Sel,
  input  [3:0] A,
  output Coutf,
  output [3:0] Y
);

  wire fa_1_cout, fa_2_cout, fa_3_cout, xor_1_out, xor_2_out, xor_3_out, xor_4_out;

  xor xor_1 (xor_1_out, B[0], Sel);
  xor xor_2 (xor_2_out, B[1], Sel);
  FA fa_1 (.A(A[0]), .B(xor_1_out), .Cin(Sel), .Y(Y[0]), .Cout(fa_1_cout));
  xor xor_3 (xor_3_out, B[2], Sel);
  FA fa_2 (.A(A[1]), .B(xor_2_out), .Cin(fa_1_cout), .Y(Y[1]), .Cout(fa_2_cout));
  FA fa_3 (.A(A[2]), .B(xor_3_out), .Cin(fa_2_cout), .Y(Y[2]), .Cout(fa_3_cout));
  xor xor_4 (xor_4_out, B[3], Sel);
  FA fa_4 (.A(A[3]), .B(xor_4_out), .Cin(fa_3_cout), .Y(Y[3]), .Cout(Coutf));
endmodule

module BtoGC (
  input  [3:0] in_1,
  output [3:0] out_2
);

  xor xor_1 (out_2[0], in_1[0], in_1[1]);
  xor xor_2 (out_2[1], in_1[1], in_1[2]);
  xor xor_3 (out_2[2], in_1[2], in_1[3]);

  assign out_2[3] = in_1[3];
endmodule
